// Logisim project DDCA PROJECT Design and Simulation of a Digital Access Card Verification System Using XORXNOR Logic.circ as structural Verilog: 1 circuit, main circuit main
module main (
  input  CARD_ID_bit_1,
  input  AUTH_ID_bit_1,
  input  CARD_ID_bit_2,
  input  AUTH_ID_bit_2,
  input  CARD_ID_bit_3,
  input  AUTH_ID_bit_3,
  input  CARD_ID_bit_4,
  input  AUTH_ID_bit_4
);

  wire and_1_out, xnor_1_out, xnor_2_out, xnor_3_out, xnor_4_out;

  xnor xnor_1 (xnor_1_out, CARD_ID_bit_1, AUTH_ID_bit_1);
  xnor xnor_2 (xnor_2_out, CARD_ID_bit_2, AUTH_ID_bit_2);
  xnor xnor_3 (xnor_3_out, CARD_ID_bit_3, AUTH_ID_bit_3);
  xnor xnor_4 (xnor_4_out, CARD_ID_bit_4, AUTH_ID_bit_4);
  and and_1 (and_1_out, xnor_1_out, xnor_2_out, xnor_3_out, xnor_4_out);
  LED led_1 (.in(and_1_out));

  // Notes on the sheet:
  //   LED on = Access Granted 
  //   LED off = Access Denied
endmodule
