// Logisim project Smart_Home_Security_SystemP299992.circ as structural Verilog: 1 circuit, main circuit main
// Smart Home Security System
module main (
  input  Door__D,
  input  Window__W,
  input  Motion__M,
  input  Mode__0_N_1_S,
  input  Armed,
  output CountLow,
  output CountHigh,
  output Alarm
);

  wire AND_2_out, AND_out, multiplexer_1_out, OR_out, XOR_out;

  xor XOR (XOR_out, Door__D, Window__W);
  and AND (AND_out, Door__D, Window__W);
  xor XOR_2 (CountLow, XOR_out, Motion__M);
  and AND_2 (AND_2_out, XOR_out, Motion__M);
  or CountHigh_OR (CountHigh, AND_out, AND_2_out);
  or OR (OR_out, CountLow, CountHigh);
  Multiplexer #(.enable("false")) multiplexer_1 (
    .in0(CountHigh), .in1(OR_out), .out(multiplexer_1_out), .sel(Mode__0_N_1_S));
  and Arm (Alarm, multiplexer_1_out, Armed);

  // Notes on the sheet:
  //   Half-Adder 1
  //   Half-Adder 2
  //   Home automated alarm
  //   Mode Select
  //   Arm Gate
endmodule
